# Fritzing sketch Arduino_Diagram (saved by Fritzing 0.9.3b)
breadboards: 1

parts:
  Part1 = Arduino Uno (Rev3) - ICSP
  BAT1 = Battery Holders [package=battery-aa]
  S5 = Round Pushbutton
  S6 = Round Pushbutton
  S7 = Round Pushbutton
  S8 = Round Pushbutton
  R1 = Resistor [tolerance=±5% resistance=220 package="1206 [SMD]"]
  R2 = Resistor [tolerance=±5% resistance=220 package="1206 [SMD]"]
  R3 = Resistor [tolerance=±5% resistance=220 package="1206 [SMD]"]
  R4 = Resistor [tolerance=±5% resistance=220 package="1206 [SMD]"]

nets:
  N1: Part1.D2, S5.leg0, R1.Pin_0
  N2: Part1.D3_PWM, S6.leg0, R2.Pin_0
  N3: Part1.D4, S7.leg0, R3.Pin_0
  N4: Part1.D5_PWM, S8.leg0, R4.Pin_0
  N5: Part1.5V, R1.Pin_1, R2.Pin_1, R3.Pin_1
  N6: Part1.GND, BAT1.-, S6.leg1, S7.leg1, S8.leg1
  N7: Part1.VIN, BAT1.+
