# Fritzing sketch Arduino_Diagram_Updated (saved by Fritzing 0.9.3b)
breadboards: 1

parts:
  Part1 = Arduino Uno (Rev3) - ICSP
  BAT1 = Battery Holders [package=battery-aa]
  R1 = Resistor [tolerance=±5% resistance=220 package="1206 [SMD]"]
  R2 = Resistor [tolerance=±5% resistance=220 package="1206 [SMD]"]
  R3 = Resistor [tolerance=±5% resistance=220 package="1206 [SMD]"]
  R4 = Resistor [tolerance=±5% resistance=220 package="1206 [SMD]"]
  S9 = Pushbutton [package="[THT]"]
  S10 = Pushbutton [package="[THT]"]
  S11 = Pushbutton [package="[THT]"]
  S12 = Pushbutton [package="[THT]"]

nets:
  N1: Part1.D2, R1.Pin_0, S9.Pin_3, S9.Pin_4
  N2: Part1.D3_PWM, R2.Pin_0, S10.Pin_3, S10.Pin_4
  N3: Part1.D4, R3.Pin_0, S11.Pin_3, S11.Pin_4
  N4: Part1.D5_PWM, R4.Pin_0, S12.Pin_3, S12.Pin_4
  N5: Part1.5V, R1.Pin_1, R2.Pin_1, R3.Pin_1
  N6: Part1.GND, BAT1.-, S9.Pin_1, S9.Pin_2, S10.Pin_1, S10.Pin_2, S11.Pin_1, S11.Pin_2, S12.Pin_1, S12.Pin_2
  N7: Part1.VIN, BAT1.+
