# Fritzing sketch Final_Diagram (saved by Fritzing 0.9.3b)
breadboards: 1

parts:
  Part1 = Arduino Uno (Rev3) - ICSP
  S1 = Pushbutton [package="[SMD]"]
  R1 = Resistor [tolerance=±5% resistance=220 package="2512 [SMD]"]
  S2 = Pushbutton [package="[SMD]"]
  R2 = Resistor [tolerance=±5% resistance=220 package="2512 [SMD]"]
  S3 = Pushbutton [package="[SMD]"]
  R3 = Resistor [tolerance=±5% resistance=220 package="2512 [SMD]"]
  S4 = Pushbutton [package="[SMD]"]
  R4 = Resistor [tolerance=±5% resistance=220 package="2512 [SMD]"]
  J1 = Dagu DGServo 9g header connector (female) [package=THT]
  J2 = Dagu DGServo 9g header connector (female) [package=THT]

nets:
  N1: Part1.5V, S1.Pin_3, S1.Pin_4, R1.Pin_1, S2.Pin_3, S2.Pin_4, R2.Pin_1, S3.Pin_3, S3.Pin_4, R3.Pin_1, S4.Pin_3, S4.Pin_4, R4.Pin_1
  N2: S1.Pin_1, S1.Pin_2, R1.Pin_0, J2.gnd
  N3: S2.Pin_1, S2.Pin_2, R2.Pin_0, J1.pulse
  N4: S3.Pin_1, S3.Pin_2, R3.Pin_0, J1.Vcc
  N5: S4.Pin_1, S4.Pin_2, R4.Pin_0, J1.gnd
